# Fritzing sketch Individual Project (saved by Fritzing 0.9.3b)
breadboards: 2

parts:
  Part2 = Arduino Uno (Rev3)
  R3 = Resistor [tolerance=±5% resistance=220 package=THT]
  R4 = Resistor [tolerance=±5% resistance=220 package=THT]
  LED2 = LED - 5mm [color="Red (633nm)" package="5 mm [THT]"]
  LED3 = LED - 5mm [color="Red (633nm)" package="5 mm [THT]"]
  Ultrasonic_Sensor2 = SRF05 Ultrasonic Rangefinder
  Ultrasonic_Sensor3 = SRF05 Ultrasonic Rangefinder
  J3 = Piezo Speaker [part_number=Buzzer]
  J4 = Piezo Speaker [part_number=Buzzer]

nets:
  N1: Part2.D10_PWM/SS, J4.pin2
  N2: Part2.D11_PWM/MOSI, R3.Pin_0, R3.Pin_1, LED2.anode
  N3: Part2.D12/MISO, J3.pin2
  N4: Part2.D13/SCK, R4.Pin_0, R4.Pin_1, LED3.anode
  GND: Part2.GND, LED2.cathode, LED3.cathode, Ultrasonic_Sensor2.GND, Ultrasonic_Sensor3.GND, J3.pin1, J4.pin1
  N5: Part2.D2, Ultrasonic_Sensor2.Echo
  N6: Part2.D3_PWM, Ultrasonic_Sensor2.Trig
  N7: Part2.D4, Ultrasonic_Sensor3.Echo
  N8: Part2.D5_PWM, Ultrasonic_Sensor3.Trig
  VCC: Part2.5V, Ultrasonic_Sensor2.VCC, Ultrasonic_Sensor3.VCC

// code stored in the sketch: Individual ProjectFritz.ino
#define ECHO_PIN1 2
#define TRIG_PIN1 3
#define buzzPin1 12
#define LED_Pin1 13
#define ECHO_PIN2 4
#define TRIG_PIN2 5
#define buzzPin2 10
#define LED_Pin2 11


void setup() {
  Serial.begin(9600);
  pinMode(LED_Pin1, OUTPUT);
  pinMode(TRIG_PIN1, OUTPUT);
  pinMode(ECHO_PIN1, INPUT);
  pinMode(buzzPin1, OUTPUT);
  pinMode(LED_Pin2, OUTPUT);
  pinMode(TRIG_PIN2, OUTPUT);
  pinMode(ECHO_PIN2, INPUT);
  pinMode(buzzPin2, OUTPUT);
}

float readDistanceCM1() {
  digitalWrite(TRIG_PIN1, LOW);
  delayMicroseconds(2);
  digitalWrite(TRIG_PIN1, HIGH);
  delayMicroseconds(10);
  digitalWrite(TRIG_PIN1, LOW);
  unsigned int duration1 = pulseIn(ECHO_PIN1, HIGH);
  return duration1 * 0.034 / 2;
}

float readDistanceCM2() {
  digitalWrite(TRIG_PIN2, LOW);
  delayMicroseconds(2);
  digitalWrite(TRIG_PIN2, HIGH);
  delayMicroseconds(10);
  digitalWrite(TRIG_PIN2, LOW);
  unsigned int duration2 = pulseIn(ECHO_PIN2, HIGH);
  return duration2 * 0.034 / 2;
}

void loop() {
  float distance1 = readDistanceCM1();
  float distance2 = readDistanceCM2();

  bool isNearby1 = distance1 < 25;
  bool isNearby2 = distance2 < 25;
  
  if(isNearby1)
 { 
  digitalWrite(LED_Pin2, 1);
  tone(buzzPin2, 250, 100);
 }
  else
  {
    digitalWrite(LED_Pin2, 0);
  }
  
  if(isNearby2)
  {
  digitalWrite(LED_Pin1, 1);
  tone(buzzPin1, 250, 100);
  }
  else
  {
    digitalWrite(LED_Pin1, 0);
  }

  Serial.print("Measured distance1: ");
  Serial.println(readDistanceCM1());
  Serial.print("Measured distance2: ");
  Serial.println(readDistanceCM2());

  delay(200);
}
